# Fritzing sketch fritzing (saved by Fritzing 0.9.3b)
breadboards: 2

parts:
  Part1 = KY-015 Temperature & Humidity Sensor Module [package="Breakout board"]
  Part2 = SRF05 Ultrasonic Rangefinder
  U1 = NodeMCU V3.0

nets:
  N1: Part1.S, Part2.VCC, U1.VU
  N2: Part1.Vin, U1.D2
  N3: Part1.-, Part2.GND, U1.GND#41
  N4: Part2.Trig, U1.D4
  N5: Part2.Echo, U1.D5
  N6: U1.GND#6, U1.GND#13, U1.GND#16, U1.GND#33

notes:
  If your module generates 0 as distance, feed it with a 5V external power supply.

custom parts:
  KY-015 Temperature & Humidity Sensor Module: KY-015 temperature and humidity sensor module, provides a low-latency serial interface to measure humidity and temperature.
  NodeMCU V3.0: ESP8266 based NodeMCU
